# Fritzing sketch Simon_game (saved by Fritzing 0.9.2b)
breadboards: 1

parts:
  Raspberry_Pi1 = Raspberry Pi 2
  LED1 = LED - 5mm [color="Red (633nm)" package="5 mm [THT]"]
  R1 = Resistor [tolerance=±5% resistance=220 package=THT]
  S1 = Pushbutton [package="[THT]"]
  LED2 = LED - 5mm [color="Green (555nm)" package="5 mm [THT]"]
  R3 = Resistor [tolerance=±5% resistance=220 package=THT]
  S2 = Pushbutton [package="[THT]"]
  LED3 = LED - 5mm [color="Blue (430nm)" package="5 mm [THT]"]
  R5 = Resistor [tolerance=±5% resistance=220 package=THT]
  S3 = Pushbutton [package="[THT]"]
  LED4 = LED - 5mm [color="Yellow (585nm)" package="5 mm [THT]"]
  R7 = Resistor [tolerance=±5% resistance=220 package=THT]
  S4 = Pushbutton [package="[THT]"]

nets:
  N1: Raspberry_Pi1.GPIO17, S1.Pin_1, S1.Pin_2
  N2: Raspberry_Pi1.GPIO22, S2.Pin_1, S2.Pin_2
  N3: Raspberry_Pi1.GPIO5, S3.Pin_1, S3.Pin_2
  N4: Raspberry_Pi1.GPIO26, S4.Pin_1, S4.Pin_2
  N5: Raspberry_Pi1.GND, R1.Pin_0, S1.Pin_3, S1.Pin_4, R3.Pin_0, S2.Pin_3, S2.Pin_4, R5.Pin_0, S3.Pin_3, S3.Pin_4, R7.Pin_0, S4.Pin_3, S4.Pin_4
  N6: Raspberry_Pi1.GPIO21, LED4.anode
  N7: Raspberry_Pi1.GPIO20, LED3.anode
  N8: Raspberry_Pi1.GPIO16, LED2.anode
  N9: Raspberry_Pi1.GPIO25, LED1.anode
  N10: LED1.cathode, R1.Pin_1
  N11: LED2.cathode, R3.Pin_1
  N12: LED3.cathode, R5.Pin_1
  N13: LED4.cathode, R7.Pin_1

notes:
  GND
  GPIO25 (Pin 22)
  GPIO17 (Pin 11)
  GPIO16 (Pin 36)
  GPIO22 (Pin 15)
  GPIO5 (Pin 29)
  GPIO20 (Pin 38)
  GPIO21 (Pin 40)
  GPIO26 (Pin 37)
